# Fritzing sketch 回路図 (saved by Fritzing 0.9.5d)
breadboards: 1

parts:
  パーツ1 = Arduino Uno (Rev3)
  S2 = SWITCH-MOMENTARY-2 [package=tactile-pth-12mm]
  S3 = SWITCH-MOMENTARY-2 [package=tactile-pth-12mm]
  S1 = SWITCH-MOMENTARY-2 [package=tactile-pth-12mm]
  r2 = Resistor [tolerance=±5% resistance=10k package=THT]
  R1 = Resistor [tolerance=±5% resistance=10k package=THT]
  R3 = Resistor [tolerance=±5% resistance=10k package=THT]
  R4 = Resistor [tolerance=±5% resistance=10k package=THT]
  R5 = Resistor [tolerance=±5% resistance=10k package=THT]
  R6 = Resistor [tolerance=±5% resistance=10k package=THT]
  SP1 = SPEAKER [package=pcb_mount_speaker]
  C1 = Electrolytic Capacitor [capacitance=4.7µF package="100 mil [THT, electrolytic]"]
  L_limirt = Round Pushbutton
  R_limit = Round Pushbutton
  sens = Round Pushbutton

nets:
  N1: パーツ1.D8, R4.Pin_0, L_limirt.leg1
  N2: パーツ1.D9_PWM, R6.Pin_0, R_limit.leg1
  N3: パーツ1.D10_PWM/SS, R5.Pin_0, sens.leg1
  N4: パーツ1.D13/SCK, C1.+
  N5: パーツ1.GND, r2.Pin_1, R1.Pin_1, R3.Pin_1, SP1.-, L_limirt.leg0, R_limit.leg0, sens.leg0
  N6: パーツ1.D2, S1.1, R1.Pin_0
  N7: パーツ1.D5_PWM, S2.1, r2.Pin_0
  N8: パーツ1.D6_PWM, S3.1, R3.Pin_0
  N9: パーツ1.5V, S2.2, S3.2, S1.2, R4.Pin_1, R5.Pin_1, R6.Pin_1
  N10: SP1.+, C1.-
